# Fritzing sketch esp8266-fridge-lights (saved by Fritzing 0.9.2b)
breadboards: 1

parts:
  RGB_SMD_LED1 = SMD RGB LED (WS2812) [package=5050]
  RGB_SMD_LED2 = SMD RGB LED (WS2812) [package=5050]
  RGB_SMD_LED3 = SMD RGB LED (WS2812) [package=5050]
  J1 = Power Jack [package=power_jack_pth_lock]
  WeMos_D1_Mini1 = WeMos D1 Mini

nets:
  N1: RGB_SMD_LED1.DIn, WeMos_D1_Mini1.D1
  VDD: RGB_SMD_LED1.VDD, RGB_SMD_LED2.VDD, RGB_SMD_LED3.VDD, J1.PWR, WeMos_D1_Mini1.5V
  VSS: RGB_SMD_LED1.VSS, RGB_SMD_LED2.VSS, RGB_SMD_LED3.VSS, J1.GND, WeMos_D1_Mini1.G
  N2: RGB_SMD_LED2.DIn, WeMos_D1_Mini1.D2
  N3: RGB_SMD_LED3.DIn, WeMos_D1_Mini1.D5

notes:
  4x 15 LEDs in zig zag
  2x 15 LEDs in zig zag
  5V power supply
